// Logisim project Making Circuits of Boolean Algebra Properties - Solution.circ as structural Verilog: 1 circuit, main circuit main
module main (
  input  a,
  input  a_2,
  input  b,
  input  c,
  input  a_3,
  input  a_4,
  input  a_5,
  input  b_2,
  input  a_6,
  input  b_3,
  input  a_7,
  input  c_2,
  input  b_4,
  input  a_8,
  input  b_5,
  input  a_9,
  input  a_10,
  output a_11,
  output F,
  output a_12,
  output F_2,
  output _1,
  output G,
  output _0,
  output G_2,
  output a_13,
  output F_3,
  output F_4,
  output a_14,
  output G_3,
  output G_4,
  output F_5,
  output a_15,
  output F_6,
  output a_16,
  output G_5,
  output F_7,
  output G_6,
  output F_8,
  output G_7,
  output G_8,
  output _1_2,
  output _0_2,
  output a_17
);

  wire and_4_out, and_7_out, and_9_out, and_10_out, and_11_out, and_12_out, and_13_out, not_1_out, not_2_out,
       not_3_out, not_4_out, not_5_out, not_6_out, not_7_out, or_4_out, or_7_out, or_9_out, or_10_out,
       or_11_out, or_12_out, or_13_out;

  not not_1 (not_1_out, a_3);
  not not_2 (not_2_out, a_3);
  or or_1 (a_11, a, a);
  and and_1 (a_12, a, a);
  or or_2 (_1, a_3, not_1_out);
  and and_2 (_0, a_3, not_2_out);
  or or_3 (a_13, a_4, 1'b0);
  and and_3 (a_14, a_4, 1'b1);
  or or_4 (or_4_out, a_6, b_3);
  or or_5 (F_5, or_4_out, c_2);
  or or_6 (F_6, a_6, or_7_out);
  or or_7 (or_7_out, b_3, c_2);
  and and_4 (and_4_out, a_6, b_3);
  and and_5 (G_5, and_4_out, c_2);
  and and_6 (G_6, a_6, and_7_out);
  and and_7 (and_7_out, b_3, c_2);
  or or_8 (_1_2, a_9, 1'b1);
  and and_8 (_0_2, a_9, 1'b0);
  not not_3 (not_3_out, a_8);
  not not_4 (not_4_out, b_5);
  and and_9 (and_9_out, a_8, b_5);
  not not_5 (not_5_out, a_8);
  not not_6 (not_6_out, b_5);
  or or_9 (or_9_out, a_8, b_5);
  not not_7 (not_7_out, a_10);
  or or_10 (or_10_out, b, c);
  and and_10 (and_10_out, a_2, b);
  and and_11 (and_11_out, a_2, c);
  and and_12 (and_12_out, b, c);
  or or_11 (or_11_out, a_2, b);
  or or_12 (or_12_out, a_2, c);
  and and_13 (and_13_out, a_7, b_4);
  or or_13 (or_13_out, a_7, b_4);
  not not_8 (F_8, and_9_out);
  not not_9 (G_8, or_9_out);
  not not_10 (a_17, not_7_out);
  and and_14 (F, a_2, or_10_out);
  or or_14 (F_2, and_10_out, and_11_out);
  or or_15 (G, a_2, and_12_out);
  and and_15 (G_2, or_11_out, or_12_out);
  or or_16 (F_3, a_5, b_2);
  or or_17 (F_4, b_2, a_5);
  and and_16 (G_3, a_5, b_2);
  and and_17 (G_4, b_2, a_5);
  or or_18 (a_15, a_7, and_13_out);
  and and_18 (a_16, a_7, or_13_out);
  or or_19 (F_7, not_3_out, not_4_out);
  and and_19 (G_7, not_5_out, not_6_out);

  // Notes on the sheet:
  //   Idempotence
  //   Complementation
  //   a'
  //   a'
  //   Identity
  //   0
  //   1
  //   Associativity
  //   a + a
  //   a * a
  //   a + a'
  //   a * a'
  //   a + 0
  //   a * 1
  //   a + b
  //   b + c
  //   a * b
  //   b * c
  //   Annihiliator
  //   a + 1
  //   1
  //   a * 0
  //   0
  //   (a + b) + c
  //   a + (b + c)
  //   (a * b) * c
  //   a * (b * c)
  //   a'
  //   b'
  //   a'
  //   b'
  //   a'
  //   Distributivity
  //   b + c
  //   a * b
  //   a * c
  //   b * c
  //   a + b
  //   a + c
  //   Commutativity
  //   Absorption
  //   a * b
  //   a + b
  //   De Morgan
  //   a * b
  //   a + b
  //   Double Negation
  //   a * (b + c)
  //   (a * b) + (a * c)
  //   a + (b * c)
  //   (a + b) * (a + c)
  //   a + b
  //   b + a
  //   a * b
  //   b * a
  //   a + (a * b)
  //   a * (a + b)
  //   a' + b'
  //   (a * b)'
  //   a' * b'
  //   (a + b)'
  //   (a')'
endmodule
