// Logisim project An automatic car - solution.circ as structural Verilog: 1 circuit, main circuit main
module main (
  input  T,
  input  X,
  output [1:0] Displayed_State,
  output [1:0] Current_State
);

  wire clock_1_out, n0_2_out, n0_3_out, n0_4_out, n0_5_out, n1_2_out, n1_3_out;
  wire [1:0] n0_out;

  or n1 (n0_out[1], n1_2_out, n1_3_out);
  Register #(.width(2)) register_1 (.D(n0_out), .Q(Current_State), .clk(clock_1_out));  // open: en, clr
  Clock clock_1 (.out(clock_1_out));
  and n1_2 (n1_2_out, ~Current_State[1], Current_State[0], T, ~X);  // AND_Gate
  and n1_3 (n1_3_out, Current_State[1], ~Current_State[0], T, ~X);  // AND_Gate
  Multiplexer #(.select(2), .width(2)) multiplexer_1 (
    .in0(2'b11), .in1(2'b01), .in2(2'b00), .out(Displayed_State), .sel(Current_State));  // open: in3, en
  or n0 (n0_out[0], n0_2_out, n0_3_out, n0_4_out, n0_5_out);
  and n0_2 (n0_2_out, ~Current_State[0], ~Current_State[1], ~T, ~X);  // AND_Gate
  and n0_3 (n0_3_out, ~Current_State[0], ~Current_State[1], T, ~X);  // AND_Gate
  and n0_4 (n0_4_out, ~Current_State[0], Current_State[1], ~T, ~X);  // AND_Gate
  and n0_5 (n0_5_out, Current_State[0], ~Current_State[1], ~T, ~X);  // AND_Gate
endmodule
