// Logisim project SER232-Assignment7-Template.circ as structural Verilog: 3 circuits, main circuit Datapath
module Datapath (
  input  [3:0] value,
  input  [1:0] write_select,
  input  [2:0] op_select,
  input  [1:0] num_1_select,
  input  [1:0] num_2_select
);

  wire clock_1_out;
  wire [3:0] register_file_1_number_1, register_file_1_number_2, undriven;

  Clock clock_1 (.out(clock_1_out));
  Register_File register_file_1 (
    .in(value), .write_select(write_select), .clk(clock_1_out), .num_1_select(num_1_select),
    .num_2_select(num_2_select), .number_1(register_file_1_number_1), .number_2(register_file_1_number_2));
  Hex_Digit_Display hex_digit_display_1 (.value(register_file_1_number_1));  // open: dp
  Hex_Digit_Display hex_digit_display_2 (.value(register_file_1_number_2));  // open: dp
  ALU alu_1 ();
  Hex_Digit_Display hex_digit_display_3 (.value(undriven));  // open: dp

  // Notes on the sheet:
  //   number 1
  //   <selected operation>
  //   number 2
  //   result
  //   =
endmodule

// RegFile
module Register_File (
  input  [3:0] in,
  input  [1:0] write_select,
  input  clk,
  input  [1:0] num_1_select,
  input  [1:0] num_2_select,
  output [3:0] number_1,
  output [3:0] number_2
);
endmodule

module ALU (
);


  // Notes on the sheet:
  //   This circuit is empty on purpose.
endmodule
