// Logisim project SER232-Assignment3-Template.circ as structural Verilog: 5 circuits, main circuit Verification Circuit
module Verification_Circuit (
  input  [2:0] i
);

  wire [3:0] undriven;

  _3x8_Decoder u_3x8_decoder_1 (.a(i));  // open: e0, e1, e2, e3, e4, e5, e6, e7
  _4_bit_1x8_Demux u_4_bit_1x8_demux_1 (.i(undriven), .s(i));  // open: d0, d1, d2, d3, d4, d5, d6, d7
  Hex_Digit_Display hex_digit_display_1 ();  // open: value, dp
  Hex_Digit_Display hex_digit_display_2 ();  // open: value, dp
  Hex_Digit_Display hex_digit_display_3 ();  // open: value, dp
  Hex_Digit_Display hex_digit_display_4 ();  // open: value, dp
  Hex_Digit_Display hex_digit_display_5 ();  // open: value, dp
  Hex_Digit_Display hex_digit_display_6 ();  // open: value, dp
  Hex_Digit_Display hex_digit_display_7 ();  // open: value, dp
  Hex_Digit_Display hex_digit_display_8 ();  // open: value, dp

  // Notes on the sheet:
  //   3x8 Decoder
  //   4-bit 1x8 Demux
  //   Hex 7 ...
  //   ... Hex 0
endmodule

module _3x8_Decoder (
  input  [2:0] a,
  output e0,
  output e1,
  output e2,
  output e3,
  output e4,
  output e5,
  output e6,
  output e7
);
endmodule

module _1_bit_1x8_Demux (
  input  i,
  input  [2:0] s,
  output d0,
  output d1,
  output d2,
  output d3,
  output d4,
  output d5,
  output d6,
  output d7
);
endmodule

module _2_bit_1x8_Demux (
  input  [1:0] i,
  input  [2:0] s,
  output [1:0] d0,
  output [1:0] d1,
  output [1:0] d2,
  output [1:0] d3,
  output [1:0] d4,
  output [1:0] d5,
  output [1:0] d6,
  output [1:0] d7
);

  _1_bit_1x8_Demux u_1_bit_1x8_demux_1 (
    .i(i[0]), .s(s), .d0(d0[0]), .d1(d1[0]), .d2(d2[0]), .d3(d3[0]), .d4(d4[0]), .d5(d5[0]), .d6(d6[0]),
    .d7(d7[0]));
  _1_bit_1x8_Demux u_1_bit_1x8_demux_2 (
    .i(i[1]), .s(s), .d0(d0[1]), .d1(d1[1]), .d2(d2[1]), .d3(d3[1]), .d4(d4[1]), .d5(d5[1]), .d6(d6[1]),
    .d7(d7[1]));
endmodule

module _4_bit_1x8_Demux (
  input  [3:0] i,
  input  [2:0] s,
  output [3:0] d0,
  output [3:0] d1,
  output [3:0] d2,
  output [3:0] d3,
  output [3:0] d4,
  output [3:0] d5,
  output [3:0] d6,
  output [3:0] d7
);

  _2_bit_1x8_Demux u_2_bit_1x8_demux_1 (
    .i(i[1:0]), .s(s), .d0(d0[1:0]), .d1(d1[1:0]), .d2(d2[1:0]), .d3(d3[1:0]), .d4(d4[1:0]), .d5(d5[1:0]),
    .d6(d6[1:0]), .d7(d7[1:0]));
  _2_bit_1x8_Demux u_2_bit_1x8_demux_2 (
    .i(i[3:2]), .s(s), .d0(d0[3:2]), .d1(d1[3:2]), .d2(d2[3:2]), .d3(d3[3:2]), .d4(d4[3:2]), .d5(d5[3:2]),
    .d6(d6[3:2]), .d7(d7[3:2]));
endmodule
