// Logisim project SER232_6 - FSM Online Session Solution.circ as structural Verilog: 1 circuit, main circuit main
module main (
  input  x,
  input  y,
  output F,
  output G,
  output H
);

  wire and_1_out, and_2_out, and_3_out, and_4_out, and_5_out, and_6_out, and_7_out, and_8_out, and_10_out,
       and_11_out, clock_1_out;
  wire [1:0] n0_out, register_1_q;

  Register #(.width(2)) register_1 (.D(n0_out), .Q(register_1_q), .clk(clock_1_out));  // open: en, clr
  Clock clock_1 (.out(clock_1_out));
  or n1 (n0_out[1], and_1_out, and_2_out, and_3_out, and_4_out);
  and and_1 (and_1_out, ~register_1_q[1], ~register_1_q[0], x, ~y);  // AND_Gate
  and and_2 (and_2_out, register_1_q[1], ~register_1_q[0], ~x, ~y);  // AND_Gate
  and and_3 (and_3_out, register_1_q[1], ~register_1_q[0], x, y);  // AND_Gate
  and and_4 (and_4_out, ~register_1_q[1], register_1_q[0], ~x, y);  // AND_Gate
  and and_5 (and_5_out, ~register_1_q[1], ~register_1_q[0], ~x, y);  // AND_Gate
  and and_6 (and_6_out, register_1_q[1], ~register_1_q[0], x, ~y);  // AND_Gate
  and and_7 (and_7_out, ~register_1_q[1], register_1_q[0], ~x, ~y);  // AND_Gate
  and and_8 (and_8_out, ~register_1_q[1], register_1_q[0], x, y);  // AND_Gate
  and and_9 (F, ~register_1_q[1], ~register_1_q[0]);  // AND_Gate
  and and_10 (and_10_out, ~register_1_q[1], ~register_1_q[0]);  // AND_Gate
  or or_1 (H, and_10_out, and_11_out);
  and and_11 (and_11_out, ~register_1_q[1], register_1_q[0]);  // AND_Gate
  or n0 (n0_out[0], and_5_out, and_6_out, and_7_out, and_8_out);

  assign G = F;

  // Notes on the sheet:
  //   next state
  //   n1 = c1'c0'xy' + c1c0'x'y' + c1c0'xy + c1'c0x'y
  //   current state
  //   c1 c0 x y
  //   F = c1'c0'
  //   G = c1'c0'
  //   H = c1'c0' + c1'c0 
  //   n0 = c1'c0'x'y + c1c0'xy' + c1'c0x'y' + c1'c0xy
endmodule
